# Fritzing sketch alarmni sustav (saved by Fritzing 0.9.3b)

parts:
  Part1 = HC-SR501 Body Sensor Module
  e-radionica_com1 = LM393 LDR breakout [part_number=100027]
  e-radionica_com2 = LM393 vibration sensor breakout [part_number=100031]
  e-radionica_com3 = LM393 hall sensor breakout [part_number=100029]
  Croduino_Basic1 = Croduino Basic2
  S1 = Round Pushbutton  # not connected
  R1 = Resistor [tolerance=±5% resistance=220 package=THT]
  KY-2 = Keyes Relay [package=THT]

nets:
  N1: Part1.OUT, Croduino_Basic1.D1_/TX
  N2: e-radionica_com1.DO, Croduino_Basic1.D3_/PWM
  VCC: e-radionica_com2.VCC, e-radionica_com3.VCC
  GND: e-radionica_com2.GND, e-radionica_com3.GND
  N3: e-radionica_com2.DO, Croduino_Basic1.D2
  N4: e-radionica_com3.DO, Croduino_Basic1.D4
  N5: Croduino_Basic1.D6_/PWM, KY-2.power
  N6: Croduino_Basic1.D5_/PWM, R1.Pin_1

custom parts:
  HC-SR501 Body Sensor Module: Pyroelectric Infrared PIR Motion Sensor Detector Module
  Croduino Basic2: Croduino Basic2 is an Arduino compatible development board with ATmega328 and CP2102.
  Keyes Relay: The Keyes 5V relay module is suitable for SCM development, home appliance control. It uses a 5V~12V TIL control signal which can control DC / AC signal.
