# Fritzing sketch hladnjak shema (saved by Fritzing 0.9.3b)

parts:
  Part2 = Arduino Mega 2560 (Rev3)
  M1 = fc-51 [package=THT]
  M2 = fc-51 [package=THT]
  M3 = fc-51 [package=THT]
  M4 = fc-51 [package=THT]
  M5 = fc-51 [package=THT]
  M6 = fc-51 [package=THT]
  Part5 = BMP180 Breakout (GY-68)
  HC-7 = Bluetooth HC-05 Macho
  Relay_5V1 = Keyes Relay [package=THT]
  Relay_5V2 = Keyes Relay [package=THT]
  M7 = fc-51 [package=THT]

nets:
  N1: Part2.A0, Relay_5V1.signal
  N2: Part2.A1, Relay_5V2.signal
  N3: Part2.A2, M7.pin1
  N4: Part2.A4, Part5.SDA
  N5: Part2.A5, Part5.SCL
  N6: Part2.D0_RX0, HC-7.TXD
  N7: Part2.D1_TX0, HC-7.RXD
  N8: Part2.D2_PWM, M4.pin1
  N9: Part2.D3_PWM, M5.pin1
  N10: Part2.D4_PWM, M1.pin1
  N11: Part2.D5_PWM, M3.pin1
  N12: Part2.D6_PWM, M2.pin1
  N13: Part2.D7_PWM, M6.pin1
  N14: M4.pin2, M6.pin2
  N15: M4.pin3, M6.pin3
  N16: Relay_5V1.ground, Relay_5V2.ground

custom parts:
  BMP180 Breakout (GY-68): This is a simple breakout board for the BMP180, a high-precision, low-power barometric pressure sensor made by Bosch Sensortec. The range of measurement is from 300hPa to 1100hPa. The sensor can be supplied with voltage ranging from 1.8V to 3.6V. Operating temperature range is -40 to +85 °C. This particular breakout board (or perhaps the configuration) is produced by Shenzhen Keep Power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
  Keyes Relay: The Keyes 5V relay module is suitable for SCM development, home appliance control. It uses a 5V~12V TIL control signal which can control DC / AC signal.
