# Fritzing sketch cuvar biljaka (saved by Fritzing 0.9.3b)

parts:
  Part1 = Arduino Nano (Rev3.0)
  DHT1 = DHT11 Humitidy and Temperature Sensor
  U3 = RELAY [package=relay-jzc]
  Part2 = Soil Moisture Sensor
  R1 = Resistor [tolerance=±5% resistance=220 package="0603 [SMD]"]
  U2 = RELAY [package=relay-jzc]
  M1 = DC Motor  # not connected
  LED2 = LED - 5mm [color="Red (633nm)" package="5 mm [THT]"]  # not connected

nets:
  GND: Part1.GND, DHT1.GND, U2.MAIN
  N1: Part1.D4, U2.COIL1
  N2: Part1.D5, U3.COIL1
  5V: Part1.5V, DHT1.VDD, R1.Pin_0
  N3: Part1.A1, Part2.SIG
  N4: Part1.A0, DHT1.DATA, R1.Pin_1

custom parts:
  DHT11 Humitidy and Temperature Sensor: DHT11 Humidity and Temperature Sensor
