# Fritzing sketch mjerac udaljenosti (saved by Fritzing 0.9.3b)

parts:
  hc-sr1 = hc-sr04
  Part1 = Arduino Nano (Rev3.0)
  OLED1 = 128x32 I2C Monochrome OLED Display

nets:
  VCC: hc-sr1.VCC, Part1.5V
  N1: hc-sr1.Trig, Part1.D11/MOSI
  N2: hc-sr1.Echo, Part1.D12/MISO
  GND: hc-sr1.GND, Part1.GND, OLED1.GND
  N3: Part1.A5, OLED1.SCL
  N4: Part1.A4, OLED1.SDA
